# Fritzing sketch Ofer (saved by Fritzing 0.9.2b)
breadboards: 1

parts:
  Pro_Micro1 = Pro Micro
  PIR1 = PIR sensor
  J1 = Basic Servo
  Part1 = Power Cell LiPo Charger/Booster
  U2 = LIPO-2000mAh [package=lipo-2000]

nets:
  GND: Pro_Micro1.GND, PIR1.GND, J1.gnd, Part1.GND, U2.-
  N1: Pro_Micro1.D4, J1.pulse
  N2: Pro_Micro1.D6, PIR1.SIG
  VCC: Pro_Micro1.VCC, PIR1.VDD, J1.vcc, Part1.VCC
  N3: Part1.VBATT, U2.+

custom parts:
  Pro Micro: The SparkFun Pro Micro is a complete USB-based microcontoller development system, in a very small footprint, capable of implementing many types of projects. All programming can be done via the USB port.
